# Fritzing sketch scale (saved by Fritzing 0.9.9b)

parts:
  Part1 = HX711 Weighing Sensor Module
  LCD1 = 1_54in tft lcd
  WeMos_D1_Mini1 = WeMos D1 Mini
  Part2 = HX711 Weighing Sensor Module
  Part3 = HX711 Weighing Sensor Module

nets:
  VCC: Part1.VCC, LCD1.pin2, WeMos_D1_Mini1.3V3
  GND: Part1.GND, LCD1.pin_1, WeMos_D1_Mini1.G, Part2.GND, Part3.GND
  N1: Part1.DO/RX, WeMos_D1_Mini1.D6
  N2: Part1.CK/TX, WeMos_D1_Mini1.D8
  N3: LCD1.pin3, WeMos_D1_Mini1.D5
  N4: LCD1.pin4, WeMos_D1_Mini1.D7
  N5: LCD1.pin_5, WeMos_D1_Mini1.A0
  N6: LCD1.pin_6, WeMos_D1_Mini1.D0
  N7: WeMos_D1_Mini1.D1, Part3.CK/TX
  N8: WeMos_D1_Mini1.D2, Part3.DO/RX
  N9: WeMos_D1_Mini1.D3, Part2.CK/TX
  N10: WeMos_D1_Mini1.D4, Part2.DO/RX
  VCC_2: Part2.VCC, Part3.VCC

custom parts:
  1_54in tft lcd: This is the DONGKER 1.54'' LCD Display Module, SPI 240x240 1.54'' LCD Display Module ST7789 Driver 240x240 3.3V IPS LCD Display Screen Module. The 1.54" display has 240x240 color pixels.
